// Digital circuit max2.dig as structural Verilog
module max2 (
  input  a0,
  input  a1,
  input  b0,
  input  b1,
  output r1,
  output r0
);

  wire and_1_out, and_2_out, and_3_out, and_4_out, and_5_out, and_6_out, and_7_out, and_8_out, and_9_out,
       and_10_out, and_11_out, and_12_out, and_13_out, and_14_out, and_15_out;

  and and_1 (and_1_out, ~a1, ~a0, ~b1, b0);  // And
  and and_2 (and_2_out, ~a1, ~a0, b1, ~b0);  // And
  and and_3 (and_3_out, ~a1, ~a0, b1, b0);  // And
  and and_4 (and_4_out, ~a1, a0, ~b1, ~b0);  // And
  and and_5 (and_5_out, ~a1, a0, ~b1, b0);  // And
  and and_6 (and_6_out, ~a1, a0, b1, ~b0);  // And
  and and_7 (and_7_out, ~a1, a0, b1, b0);  // And
  and and_8 (and_8_out, a1, ~a0, ~b1, ~b0);  // And
  and and_9 (and_9_out, a1, ~a0, ~b1, b0);  // And
  and and_10 (and_10_out, a1, ~a0, b1, ~b0);  // And
  and and_11 (and_11_out, a1, ~a0, b1, b0);  // And
  and and_12 (and_12_out, a1, a0, ~b1, ~b0);  // And
  and and_13 (and_13_out, a1, a0, ~b1, b0);  // And
  and and_14 (and_14_out, a1, a0, b1, ~b0);  // And
  and and_15 (and_15_out, a1, a0, b1, b0);
  or or_1 (r1, and_2_out, and_3_out, and_6_out, and_7_out, and_8_out, and_9_out, and_10_out, and_11_out, and_12_out, and_13_out, and_14_out, and_15_out);
  or or_2 (r0, and_1_out, and_3_out, and_4_out, and_5_out, and_7_out, and_11_out, and_12_out, and_13_out, and_14_out, and_15_out);
endmodule
