// Digital circuit inst_memory.dig as structural Verilog
module inst_memory (
  input  [7:0] ADDR,
  input  [1:0] PROG,
  output [31:0] IW
);

  wire [31:0] rom_1_d, rom_2_d, rom_3_d, rom_4_d;

  ROM #(.AddrBits(8), .Bits(32)) rom_1 (.A(ADDR), .sel(1'b1), .D(rom_1_d));
  ROM #(.AddrBits(8), .Bits(32)) rom_2 (.A(ADDR), .sel(1'b1), .D(rom_2_d));
  ROM #(.AddrBits(8), .Bits(32)) rom_3 (.A(ADDR), .sel(1'b1), .D(rom_3_d));
  ROM #(.AddrBits(8), .Bits(32)) rom_4 (.A(ADDR), .sel(1'b1), .D(rom_4_d));
  Multiplexer #(.Selector_Bits(2), .Bits(32)) multiplexer_1 (
    .sel(PROG), .in_0(rom_1_d), .in_1(rom_2_d), .in_2(rom_3_d), .in_3(rom_4_d), .out(IW));

  // Notes on the sheet:
  //   contents of rom_1 (hex, n*v repeats v):
  //   100293,a2c463,8067,fe810113,113023,a13423,fff50513,fe5ff0ef,a13823
  //   ,813503,ffe50513,fd5ff0ef,1013303,650533,13083,1810113,8067,c0001073
  //   contents of rom_2 (hex, n*v repeats v):
  //   c5c663,100513,3c0006f,b502b3,28283,c50333,30303,628663,513,200006f
  //   ,ff810113,113023,158593,fff60613,fc9ff0ef,13083,810113,8067,c0001073
  //   contents of rom_3 (hex, n*v repeats v):
  //   40b602b3,128293,4000393,729863,50313,fff00393,140006f,b55333,100393
  //   ,5393b3,fff38393,737533,8067,c0001073
  //   contents of rom_4 (hex, n*v repeats v):
  //   2a502b3,2b282b3,2c50333,628533,d50533,8067,c0001073
endmodule
