// Digital circuit lab06.dig as structural Verilog
module lab06 (
  input  [1:0] ALUOp,
  input  ALUSrcB,
  input  [63:0] Imm,
  input  [4:0] RR0,
  input  [4:0] RR1,
  input  [4:0] WR,
  input  WE,
  input  CLK,
  input  [1:0] PROG,
  input  CLR,
  output [63:0] T0,
  output [63:0] T1
);

  wire [31:0] iw;
  wire [63:0] alu_1_r, multiplexer_1_out, pc_1_q, PC_plus_4_s, register_file_1_rd0, register_file_1_rd1, x0,
       x1, x2, x3, x4, x7, x8, x9, x10, x11, x12, x13, x14, x15, x16, x17, x18, x19, x20, x21, x22, x23, x24,
       x25, x26, x27, x28, x29, x30, x31;

  pc pc_1 (.D(PC_plus_4_s), .CLK(CLK), .EN(1'b1), .CLR(CLR), .Q(pc_1_q));
  inst_memory inst_memory_1 (.ADDR(pc_1_q[9:2]), .PROG(PROG), .IW(iw));
  Add #(.Bits(64)) PC_plus_4 (.a(pc_1_q), .b(64'h4), .c_i(1'b0), .s(PC_plus_4_s));  // open: c_o
  register_file register_file_1 (
    .ReadReg0(RR0), .ReadReg1(RR1), .WriteData(alu_1_r), .CLK(CLK), .WriteEn(WE), .CLR(CLR), .WriteReg(WR),
    .RD0(register_file_1_rd0), .RD1(register_file_1_rd1), .x0(x0), .x1(x1), .x2(x2), .x3(x3), .x4(x4),
    .x5(T0), .x6(T1), .x7(x7), .x8(x8), .x9(x9), .x10(x10), .x11(x11), .x12(x12), .x13(x13), .x14(x14),
    .x15(x15), .x16(x16), .x17(x17), .x18(x18), .x19(x19), .x20(x20), .x21(x21), .x22(x22), .x23(x23),
    .x24(x24), .x25(x25), .x26(x26), .x27(x27), .x28(x28), .x29(x29), .x30(x30), .x31(x31));
  Multiplexer #(.Bits(64)) multiplexer_1 (
    .sel(ALUSrcB), .in_0(register_file_1_rd1), .in_1(Imm), .out(multiplexer_1_out));
  alu alu_1 (.A(register_file_1_rd0), .B(multiplexer_1_out), .ALUOp(ALUOp), .R(alu_1_r));

  // Other names for the same wires on the sheet: x5[63:0] = T0; x6[63:0] = T1
endmodule
