// Digital circuit register_file.dig as structural Verilog
module register_file (
  input  [4:0] ReadReg0,
  input  [4:0] ReadReg1,
  input  [4:0] WriteReg,
  input  WriteEn,
  input  [63:0] WriteData,
  input  CLK,
  input  CLR,
  output [63:0] RD0,
  output [63:0] RD1,
  output [63:0] x1,
  output [63:0] x2,
  output [63:0] x3,
  output [63:0] x4,
  output [63:0] x5,
  output [63:0] x6,
  output [63:0] x7,
  output [63:0] x8,
  output [63:0] x9,
  output [63:0] x10,
  output [63:0] x11,
  output [63:0] x12,
  output [63:0] x13,
  output [63:0] x14,
  output [63:0] x15,
  output [63:0] x16,
  output [63:0] x17,
  output [63:0] x18,
  output [63:0] x19,
  output [63:0] x20,
  output [63:0] x21,
  output [63:0] x22,
  output [63:0] x23,
  output [63:0] x24,
  output [63:0] x25,
  output [63:0] x26,
  output [63:0] x27,
  output [63:0] x28,
  output [63:0] x29,
  output [63:0] x30,
  output [63:0] x31,
  output [63:0] x0
);

  wire decoder_1_out_1, decoder_1_out_2, decoder_1_out_3, decoder_1_out_4, decoder_1_out_5, decoder_1_out_6,
       decoder_1_out_7, decoder_1_out_8, decoder_1_out_9, decoder_1_out_10, decoder_1_out_11,
       decoder_1_out_12, decoder_1_out_13, decoder_1_out_14, decoder_1_out_15, decoder_1_out_16,
       decoder_1_out_17, decoder_1_out_18, decoder_1_out_19, decoder_1_out_20, decoder_1_out_21,
       decoder_1_out_22, decoder_1_out_23, decoder_1_out_24, decoder_1_out_25, decoder_1_out_26,
       decoder_1_out_27, decoder_1_out_28, decoder_1_out_29, decoder_1_out_30, decoder_1_out_31;
  wire [4:0] multiplexer_1_out;

  Multiplexer #(.Bits(5)) multiplexer_1 (.sel(WriteEn), .in_0({5{1'b0}}), .in_1(WriteReg), .out(multiplexer_1_out));
  Decoder #(.Selector_Bits(5)) decoder_1 (
    .sel(multiplexer_1_out), .out_1(decoder_1_out_1), .out_2(decoder_1_out_2), .out_3(decoder_1_out_3),
    .out_4(decoder_1_out_4), .out_5(decoder_1_out_5), .out_6(decoder_1_out_6), .out_7(decoder_1_out_7),
    .out_8(decoder_1_out_8), .out_9(decoder_1_out_9), .out_10(decoder_1_out_10), .out_11(decoder_1_out_11),
    .out_12(decoder_1_out_12), .out_13(decoder_1_out_13), .out_14(decoder_1_out_14),
    .out_15(decoder_1_out_15), .out_16(decoder_1_out_16), .out_17(decoder_1_out_17),
    .out_18(decoder_1_out_18), .out_19(decoder_1_out_19), .out_20(decoder_1_out_20),
    .out_21(decoder_1_out_21), .out_22(decoder_1_out_22), .out_23(decoder_1_out_23),
    .out_24(decoder_1_out_24), .out_25(decoder_1_out_25), .out_26(decoder_1_out_26),
    .out_27(decoder_1_out_27), .out_28(decoder_1_out_28), .out_29(decoder_1_out_29),
    .out_30(decoder_1_out_30), .out_31(decoder_1_out_31));  // open: out_0
  // _64_reg_clr x1: pin names not known; wires that end beside it: WriteData, CLK, decoder_1_out_1, CLR, x1
  // _64_reg_clr x2: pin names not known; wires that end beside it: WriteData, CLK, decoder_1_out_2, CLR, x2
  // _64_reg_clr x3: pin names not known; wires that end beside it: WriteData, CLK, decoder_1_out_3, CLR, x3
  // _64_reg_clr x4: pin names not known; wires that end beside it: WriteData, CLK, decoder_1_out_4, CLR, x4
  // _64_reg_clr x5: pin names not known; wires that end beside it: WriteData, CLK, decoder_1_out_5, CLR, x5
  // _64_reg_clr x6: pin names not known; wires that end beside it: WriteData, CLK, decoder_1_out_6, CLR, x6
  // _64_reg_clr x7: pin names not known; wires that end beside it: WriteData, CLK, decoder_1_out_7, CLR, x7
  // _64_reg_clr x8: pin names not known; wires that end beside it: WriteData, CLK, decoder_1_out_8, CLR, x8
  // _64_reg_clr x9: pin names not known; wires that end beside it: WriteData, CLK, decoder_1_out_9, CLR, x9
  // _64_reg_clr x10: pin names not known; wires that end beside it: WriteData, CLK, decoder_1_out_10, CLR, x10
  // _64_reg_clr x11: pin names not known; wires that end beside it: WriteData, CLK, decoder_1_out_11, CLR, x11
  // _64_reg_clr x12: pin names not known; wires that end beside it: WriteData, CLK, decoder_1_out_12, CLR, x12
  // _64_reg_clr x13: pin names not known; wires that end beside it: WriteData, CLK, decoder_1_out_13, CLR, x13
  // _64_reg_clr x14: pin names not known; wires that end beside it: WriteData, CLK, decoder_1_out_14, CLR, x14
  // _64_reg_clr x15: pin names not known; wires that end beside it: WriteData, CLK, decoder_1_out_15, CLR, x15
  // _64_reg_clr x16: pin names not known; wires that end beside it: WriteData, CLK, decoder_1_out_16, CLR, x16
  // _64_reg_clr x17: pin names not known; wires that end beside it: WriteData, CLK, decoder_1_out_17, CLR, x17
  // _64_reg_clr x18: pin names not known; wires that end beside it: WriteData, CLK, decoder_1_out_18, CLR, x18
  // _64_reg_clr x19: pin names not known; wires that end beside it: WriteData, CLK, decoder_1_out_19, CLR, x19
  // _64_reg_clr x20: pin names not known; wires that end beside it: WriteData, CLK, decoder_1_out_20, CLR, x20
  // _64_reg_clr x21: pin names not known; wires that end beside it: WriteData, CLK, decoder_1_out_21, CLR, x21
  // _64_reg_clr x22: pin names not known; wires that end beside it: WriteData, CLK, decoder_1_out_22, CLR, x22
  // _64_reg_clr x23: pin names not known; wires that end beside it: WriteData, CLK, decoder_1_out_23, CLR, x23
  // _64_reg_clr x24: pin names not known; wires that end beside it: WriteData, CLK, decoder_1_out_24, CLR, x24
  // _64_reg_clr x25: pin names not known; wires that end beside it: WriteData, CLK, decoder_1_out_25, CLR, x25
  // _64_reg_clr x26: pin names not known; wires that end beside it: WriteData, CLK, decoder_1_out_26, CLR, x26
  // _64_reg_clr x27: pin names not known; wires that end beside it: WriteData, CLK, decoder_1_out_27, CLR, x27
  // _64_reg_clr x28: pin names not known; wires that end beside it: WriteData, CLK, decoder_1_out_28, CLR, x28
  // _64_reg_clr x29: pin names not known; wires that end beside it: WriteData, CLK, decoder_1_out_29, CLR, x29
  // _64_reg_clr x30: pin names not known; wires that end beside it: WriteData, CLK, decoder_1_out_30, CLR, x30
  // _64_reg_clr x31: pin names not known; wires that end beside it: WriteData, CLK, decoder_1_out_31, CLR, x31
  Multiplexer #(.Selector_Bits(5), .Bits(64)) multiplexer_2 (
    .sel(ReadReg0), .in_0({64{1'b0}}), .in_1(x1), .in_2(x2), .in_3(x3), .in_4(x4), .in_5(x5), .in_6(x6),
    .in_7(x7), .in_8(x8), .in_9(x9), .in_10(x10), .in_11(x11), .in_12(x12), .in_13(x13), .in_14(x14),
    .in_15(x15), .in_16(x16), .in_17(x17), .in_18(x18), .in_19(x19), .in_20(x20), .in_21(x21), .in_22(x22),
    .in_23(x23), .in_24(x24), .in_25(x25), .in_26(x26), .in_27(x27), .in_28(x28), .in_29(x29), .in_30(x30),
    .in_31(x31), .out(RD0));
  Multiplexer #(.Selector_Bits(5), .Bits(64)) multiplexer_3 (
    .sel(ReadReg1), .in_0({64{1'b0}}), .in_1(x1), .in_2(x2), .in_3(x3), .in_4(x4), .in_5(x5), .in_6(x6),
    .in_7(x7), .in_8(x8), .in_9(x9), .in_10(x10), .in_11(x11), .in_12(x12), .in_13(x13), .in_14(x14),
    .in_15(x15), .in_16(x16), .in_17(x17), .in_18(x18), .in_19(x19), .in_20(x20), .in_21(x21), .in_22(x22),
    .in_23(x23), .in_24(x24), .in_25(x25), .in_26(x26), .in_27(x27), .in_28(x28), .in_29(x29), .in_30(x30),
    .in_31(x31), .out(RD1));

  assign x0 = {64{1'b0}};
endmodule
