// Digital circuit InstDecoder1.dig as structural Verilog
module InstDecoder1 (
  input  [31:0] IW,
  output [1:0] ALUSrcB,
  output [2:0] ALUOp,
  output RFW
);

  wire addi_1_eq, addr_1_eq, INUM_num;

  ADDI addi_1 (.opcode(IW[6:0]), .funct3(IW[14:12]), .EQ(addi_1_eq));
  ADDR addr_1 (.opcode(IW[6:0]), .funct3(IW[14:12]), .funct7(IW[31:25]), .EQ(addr_1_eq));
  PriorityEncoder INUM (.in0(addi_1_eq), .in1(addr_1_eq), .num(INUM_num));  // open: any
  ROM #(.AddrBits(1), .Bits(5)) rom_1 (.A(INUM_num), .sel(1'b1), .D({RFW, ALUOp, ALUSrcB[0]}));
  // Pins of 1 and 2 bits meet at ALUSrcB

  // Other names for the same wires on the sheet: opcode[6:0] = IW[6:0]; funct3[2:0] = IW[14:12];
  //   funct7[6:0] = IW[31:25]

  // Notes on the sheet:
  //   contents of rom_1 (hex, n*v repeats v):
  //   11,10,11b,83
endmodule
