// Digital circuit InstrDecoder.dig as structural Verilog
module InstrDecoder (
  input  [31:0] IW,
  output [1:0] ALUSrcB,
  output [2:0] ALUOp,
  output RFW,
  output ALUSrcA,
  output PCSel,
  output WDSel
);

  wire addi_1_eq, addr_1_eq, j_type_eq, jalr_1_eq;
  wire [1:0] INUM_num;

  ADDI addi_1 (.opcode(IW[6:0]), .funct3(IW[14:12]), .EQ(addi_1_eq));
  ADDR addr_1 (.opcode(IW[6:0]), .funct3(IW[14:12]), .funct7(IW[31:25]), .EQ(addr_1_eq));
  Comparator #(.Bits(7)) j_type (.a(IW[6:0]), .b(7'b1101111), .eq(j_type_eq));  // open: gt, lt
  JALR jalr_1 (.opcode(IW[6:0]), .funct3(IW[14:12]), .EQ(jalr_1_eq));
  PriorityEncoder #(.Selector_Bits(2)) INUM (
    .in0(addi_1_eq), .in1(addr_1_eq), .in2(j_type_eq), .in3(jalr_1_eq), .num(INUM_num));  // open: any
  ROM #(.Bits(9)) rom_1 (.A(INUM_num), .sel(1'b1), .D({RFW, ALUOp, ALUSrcA, ALUSrcB, PCSel, WDSel}));

  // Other names for the same wires on the sheet: opcode[6:0] = IW[6:0]; funct3[2:0] = IW[14:12];
  //   funct7[6:0] = IW[31:25]

  // Notes on the sheet:
  //   contents of rom_1 (hex, n*v repeats v):
  //   104,100,11b,107
endmodule
