// Digital circuit alu.dig as structural Verilog
module alu (
  input  [63:0] A,
  input  [63:0] B,
  input  [2:0] ALUOp,
  output [63:0] R
);

  wire [63:0] add_s, mul_mul, notconnected_1_out, notconnected_2_out, notconnected_3_out, sll_out, srl_out,
       sub_s;

  Add #(.Bits(64)) add (.a(A), .b(B), .c_i(1'b0), .s(add_s));  // open: c_o
  Sub #(.Bits(64)) sub (.a(A), .b(B), .c_i(1'b0), .s(sub_s));  // open: c_o
  Mul #(.Bits(32)) mul (.a(A[31:0]), .b(B[31:0]), .mul(mul_mul));
  BarrelShifter #(.Bits(64)) sll (.in(A), .shift(B[6:0]), .out(sll_out));
  BarrelShifter #(.Bits(64), .direction("right")) srl (.in(A), .shift(B[6:0]), .out(srl_out));
  Multiplexer #(.Selector_Bits(3), .Bits(64)) multiplexer_1 (
    .sel(ALUOp), .in_0(add_s), .in_1(sub_s), .in_2(mul_mul), .in_3(sll_out), .in_4(srl_out),
    .in_5(notconnected_1_out), .in_6(notconnected_2_out), .in_7(notconnected_3_out), .out(R));
  // NotConnected on notconnected_1_out
  // NotConnected on notconnected_2_out
  // NotConnected on notconnected_3_out
endmodule
