// Digital circuit inst_memory.dig as structural Verilog
module inst_memory (
  input  [7:0] ADDR,
  input  PROG,
  output [31:0] IW
);

  wire [31:0] rom_1_d, rom_2_d;

  ROM #(.AddrBits(8), .Bits(32)) rom_1 (.A(ADDR), .sel(1'b1), .D(rom_1_d));
  ROM #(.AddrBits(8), .Bits(32)) rom_2 (.A(ADDR), .sel(1'b1), .D(rom_2_d));
  Multiplexer #(.Bits(32)) multiplexer_1 (.sel(PROG), .in_0(rom_1_d), .in_1(rom_2_d), .out(IW));

  // Notes on the sheet:
  //   contents of rom_1 (hex, n*v repeats v):
  //   100513,200593,b50633,c0001073
  //   contents of rom_2 (hex, n*v repeats v):
  //   100513,200593,8000ef,c0001073,b50533,8067
endmodule
