// Digital circuit lab07-part1.dig as structural Verilog
module lab07_part1 (
  input  CLK,
  input  EN,
  input  CLR,
  input  PROG,
  output [63:0] A0,
  output [63:0] A1,
  output [63:0] A2,
  output DONE
);

  wire ALUSrcB, and_2_out, CLK_t, RFW;
  wire [2:0] ALUOp;
  wire [4:0] rd, rs1, rs2;
  wire [31:0] iw;
  wire [63:0] _64_reg_clr_1_p1, alu_1_r, imm_I, multiplexer_1_out, PC, register_file_1_rd0,
       register_file_1_rd1, x0, x1, x2, x3, x4, x5, x6, x7, x8, x9, x13, x14, x15, x16, x17, x18, x19, x20,
       x21, x22, x23, x24, x25, x26, x27, x28, x29, x30, x31;

  Comparator #(.Bits(32)) comparator_1 (.a(iw), .b(32'hc0001073), .eq(DONE));  // open: gt, lt
  // _64_reg_clr _64_reg_clr_1: pin names not known; wires that end beside it: _64_reg_clr_1_p1, CLK_t, EN, CLR, PC
  and and_1 (CLK_t, CLK, ~DONE);  // And
  // Probe on PC
  // Probe on iw
  // Probe on rs1
  // Probe on rs2
  // Probe on rd
  // Probe on imm_I
  LED led_1 (.in(DONE));
  inst_memory inst_memory_1 (.PROG(PROG), .ADDR(PC[9:2]), .IW(iw));
  Add #(.Bits(64)) add_1 (.a(PC), .b(64'h4), .c_i(1'b0), .s(_64_reg_clr_1_p1));  // open: c_o
  // Probe on x0
  // Probe on x1
  // Probe on x2
  // Probe on x3
  // Probe on x4
  // Probe on x5
  // Probe on x6
  // Probe on x7
  // InstDecoder1 instdecoder1_1: pin names not known; wires that end beside it: iw, ALUSrcB, ALUOp, RFW
  RegDecoder regdecoder_1 (.IW(iw), .RS1(rs1), .RS2(rs2), .RD(rd));
  // ImmDecoder immdecoder_1: pin names not known; wires that end beside it: iw, imm_I
  // Probe on x8
  // Probe on x9
  // Probe on A0
  // Probe on A1
  // Probe on A2
  // Probe on x13
  // Probe on x14
  // Probe on x15
  and and_2 (and_2_out, RFW, EN);
  // Probe on x16
  // Probe on x17
  // Probe on x18
  // Probe on x19
  // Probe on x20
  // Probe on x21
  // Probe on x22
  // Probe on x23
  register_file register_file_1 (
    .ReadReg0(rs1), .ReadReg1(rs2), .WriteData(alu_1_r), .CLK(CLK_t), .WriteEn(and_2_out), .CLR(CLR),
    .WriteReg(rd), .RD0(register_file_1_rd0), .RD1(register_file_1_rd1), .x0(x0), .x1(x1), .x2(x2), .x3(x3),
    .x4(x4), .x5(x5), .x6(x6), .x7(x7), .x8(x8), .x9(x9), .x10(A0), .x11(A1), .x12(A2), .x13(x13), .x14(x14),
    .x15(x15), .x16(x16), .x17(x17), .x18(x18), .x19(x19), .x20(x20), .x21(x21), .x22(x22), .x23(x23),
    .x24(x24), .x25(x25), .x26(x26), .x27(x27), .x28(x28), .x29(x29), .x30(x30), .x31(x31));
  // Probe on x24
  // Probe on x25
  // Probe on x26
  // Probe on x27
  // Probe on x28
  // Probe on x29
  // Probe on x30
  // Probe on x31
  Multiplexer #(.Bits(64)) multiplexer_1 (
    .sel(ALUSrcB), .in_0(register_file_1_rd1), .in_1(imm_I), .out(multiplexer_1_out));
  alu alu_1 (.A(register_file_1_rd0), .B(multiplexer_1_out), .ALUOp(ALUOp), .R(alu_1_r));

  // Other names for the same wires on the sheet: x10[63:0] = A0; x11[63:0] = A1; x12[63:0] = A2
endmodule
