// Digital circuit BLT.dig as structural Verilog
module BLT (
  input  [6:0] opcode,
  input  [2:0] funct3,
  output EQ
);

  wire comparator_1_eq, comparator_2_eq;

  Comparator #(.Bits(7)) comparator_1 (.a(opcode), .b(7'b1100011), .eq(comparator_1_eq));  // open: gt, lt
  Comparator #(.Bits(3)) comparator_2 (.a(funct3), .b(3'b100), .eq(comparator_2_eq));  // open: gt, lt
  and and_1 (EQ, comparator_1_eq, comparator_2_eq);
endmodule
