// Digital circuit BranchInstruct.dig as structural Verilog
module BranchInstruct (
  input  [6:0] opcode,
  input  [2:0] funct3,
  output EQ
);

  wire beq_1_eq, bge_1_eq, blt_1_eq, bne_1_eq;

  BEQ beq_1 (.opcode(opcode), .funct3(funct3), .EQ(beq_1_eq));
  BNE bne_1 (.opcode(opcode), .funct3(funct3), .EQ(bne_1_eq));
  BLT blt_1 (.opcode(opcode), .funct3(funct3), .EQ(blt_1_eq));
  BGE bge_1 (.opcode(opcode), .funct3(funct3), .EQ(bge_1_eq));
  or or_1 (EQ, beq_1_eq, bne_1_eq, blt_1_eq, bge_1_eq);
endmodule
