// Digital circuit BranchUnit.dig as structural Verilog
module BranchUnit (
  input  [63:0] RD0,
  input  [63:0] RD1,
  input  PCSEL,
  input  [2:0] BrOp,
  output PCbr
);

  wire BEQ_eq, BGE_eq, BGE_gt, BLT_lt, BNE_gt, BNE_lt, or_1_out, or_2_out, taken;

  Comparator #(.Bits(64)) BEQ (.a(RD0), .b(RD1), .eq(BEQ_eq));  // open: gt, lt
  Comparator #(.Bits(64)) BNE (.a(RD0), .b(RD1), .gt(BNE_gt), .lt(BNE_lt));  // open: eq
  Comparator #(.Bits(64)) BLT (.a(RD0), .b(RD1), .lt(BLT_lt));  // open: gt, eq
  Comparator #(.Bits(64)) BGE (.a(RD0), .b(RD1), .gt(BGE_gt), .eq(BGE_eq));  // open: lt
  or or_1 (or_1_out, BNE_gt, BNE_lt);
  or or_2 (or_2_out, BGE_gt, BGE_eq);
  or or_3 (PCbr, PCSEL, taken);
  Multiplexer #(.Selector_Bits(3)) multiplexer_1 (
    .sel(BrOp), .in_0(BEQ_eq), .in_1(or_1_out), .in_2(1'b0), .in_3(1'b0), .in_4(BLT_lt), .in_5(or_2_out),
    .in_6(1'b0), .in_7(1'b0), .out(taken));
endmodule
