// Digital circuit InstrDecoder.dig as structural Verilog
module InstrDecoder (
  input  [31:0] IW,
  output [2:0] ALUSrcB,
  output [2:0] ALUOp,
  output RFW,
  output ALUSrcA,
  output PCSel,
  output WDSel,
  output [2:0] funct3,
  output [2:0] BrOp,
  output MR,
  output STR,
  output LD
);

  wire addi_1_eq, addr_1_eq, and_1_eq, beq_1_eq, bge_1_eq, blt_1_eq, bne_1_eq, j_type_eq, jalr_1_eq,
       load_1_eq, lui_1_eq, mul_1_eq, or_1_eq, save_1_eq, slli_1_eq, sllr_1_eq, srl_1_eq, srli_1_eq, sub_1_eq;
  wire [4:0] INUM_num;

  ADDI addi_1 (.opcode(IW[6:0]), .funct3(IW[14:12]), .EQ(addi_1_eq));
  ADDR addr_1 (.opcode(IW[6:0]), .funct3(IW[14:12]), .funct7(IW[31:25]), .EQ(addr_1_eq));
  Comparator #(.Bits(7)) j_type (.a(IW[6:0]), .b(7'b1101111), .eq(j_type_eq));  // open: gt, lt
  JALR jalr_1 (.opcode(IW[6:0]), .funct3(IW[14:12]), .EQ(jalr_1_eq));
  SLLR sllr_1 (.opcode(IW[6:0]), .funct3(IW[14:12]), .funct7(IW[31:25]), .EQ(sllr_1_eq));
  SLLI slli_1 (.opcode(IW[6:0]), .funct3(IW[14:12]), .funct6(IW[31:26]), .EQ(slli_1_eq));
  SRL srl_1 (.opcode(IW[6:0]), .funct3(IW[14:12]), .funct7(IW[31:25]), .EQ(srl_1_eq));
  SRLI srli_1 (.opcode(IW[6:0]), .funct3(IW[14:12]), .funct6(IW[31:26]), .EQ(srli_1_eq));
  MUL mul_1 (.opcode(IW[6:0]), .funct3(IW[14:12]), .funct7(IW[31:25]), .EQ(mul_1_eq));
  BEQ beq_1 (.opcode(IW[6:0]), .funct3(IW[14:12]), .EQ(beq_1_eq));
  BNE bne_1 (.opcode(IW[6:0]), .funct3(IW[14:12]), .EQ(bne_1_eq));
  BLT blt_1 (.opcode(IW[6:0]), .funct3(IW[14:12]), .EQ(blt_1_eq));
  BGE bge_1 (.opcode(IW[6:0]), .funct3(IW[14:12]), .EQ(bge_1_eq));
  LUI lui_1 (.opcode(IW[6:0]), .EQ(lui_1_eq));
  Load load_1 (.opcode(IW[6:0]), .funct3(IW[14:12]), .EQ(load_1_eq));
  Save save_1 (.opcode(IW[6:0]), .funct3(IW[14:12]), .EQ(save_1_eq));
  SUB sub_1 (.opcode(IW[6:0]), .funct3(IW[14:12]), .funct7(IW[31:25]), .EQ(sub_1_eq));
  AND and_1 (.opcode(IW[6:0]), .funct3(IW[14:12]), .funct7(IW[31:25]), .EQ(and_1_eq));
  OR or_1 (.opcode(IW[6:0]), .funct3(IW[14:12]), .funct7(IW[31:25]), .EQ(or_1_eq));
  PriorityEncoder #(.Selector_Bits(5)) INUM (
    .in0(addi_1_eq), .in1(addr_1_eq), .in2(j_type_eq), .in3(jalr_1_eq), .in4(sllr_1_eq), .in5(slli_1_eq),
    .in6(srl_1_eq), .in7(srli_1_eq), .in8(mul_1_eq), .in9(beq_1_eq), .in10(bne_1_eq), .in11(blt_1_eq),
    .in12(bge_1_eq), .in13(lui_1_eq), .in14(load_1_eq), .in15(save_1_eq), .in16(sub_1_eq), .in17(and_1_eq),
    .in18(or_1_eq), .in19(1'b0), .in20(1'b0), .in21(1'b0), .in22(1'b0), .in23(1'b0), .in24(1'b0),
    .in25(1'b0), .in26(1'b0), .in27(1'b0), .in28(1'b0), .in29(1'b0), .in30(1'b0), .in31(1'b0), .num(INUM_num));  // open: any
  ROM #(.AddrBits(5), .Bits(16)) rom_1 (
    .A(INUM_num), .sel(1'b1), .D({RFW, ALUOp, ALUSrcA, ALUSrcB, PCSel, WDSel, BrOp, MR, STR, LD}));

  assign funct3 = IW[14:12];

  // Other names for the same wires on the sheet: opcode[6:0] = IW[6:0]; funct7[6:0] = IW[31:25];
  //   funct6[5:0] = IW[31:26]

  // Notes on the sheet:
  //   contents of rom_1 (hex, n*v repeats v):
  //   8130,8030,8af0,81f0,b030,b130,c030,c130,a030,b40,b48,b60,b68,d530
  //   ,8135,433,9030,e030,f030
endmodule
