// Digital circuit LUI.dig as structural Verilog
module LUI (
  input  [6:0] opcode,
  output EQ
);

  Comparator #(.Bits(7)) comparator_1 (.a(opcode), .b(7'b0110111), .eq(EQ));  // open: gt, lt
endmodule
