// Digital circuit READ_CIR.dig as structural Verilog
module READ_CIR (
  input  [63:0] Din,
  input  [63:0] A,
  input  [2:0] funct3,
  output [63:0] Dout,
  output [63:0] Dcurr
);

  wire [7:0] multiplexer_1_out;
  wire [31:0] multiplexer_2_out;
  wire [63:0] bitextender_1_out, bitextender_2_out;

  Multiplexer #(.Selector_Bits(3), .Bits(8)) multiplexer_1 (
    .sel(A[2:0]), .in_0(Din[7:0]), .in_1(Din[15:8]), .in_2(Din[23:16]), .in_3(Din[31:24]), .in_4(Din[39:32]),
    .in_5(Din[47:40]), .in_6(Din[55:48]), .in_7(Din[63:56]), .out(multiplexer_1_out));
  Multiplexer #(.Bits(32)) multiplexer_2 (.sel(A[2]), .in_0(Din[31:0]), .in_1(Din[63:32]), .out(multiplexer_2_out));
  BitExtender #(.outputBits(64)) bitextender_1 (.in(multiplexer_1_out), .out(bitextender_1_out));
  BitExtender #(.inputBits(32), .outputBits(64)) bitextender_2 (.in(multiplexer_2_out), .out(bitextender_2_out));
  Multiplexer #(.Selector_Bits(2), .Bits(64)) multiplexer_3 (
    .sel(funct3[1:0]), .in_0(bitextender_1_out), .in_1({64{1'b0}}), .in_2(bitextender_2_out), .in_3(Din),
    .out(Dout));

  assign Dcurr = Din;
endmodule
