// Digital circuit SB.dig as structural Verilog
module SB (
  input  [63:0] Din,
  input  [63:0] Dcurr,
  input  [2:0] byteInd,
  output [63:0] SB
);

  Multiplexer #(.Selector_Bits(3), .Bits(64)) multiplexer_1 (
    .sel(byteInd), .in_0({Dcurr[63:8], Din[7:0]}), .in_1({Dcurr[63:16], Din[7:0], Dcurr[7:0]}),
    .in_2({Dcurr[63:24], Din[7:0], Dcurr[15:0]}), .in_3({Dcurr[63:32], Din[7:0], Dcurr[23:0]}),
    .in_4({Dcurr[63:40], Din[7:0], Dcurr[31:0]}), .in_5({Dcurr[63:48], Din[7:0], Dcurr[39:0]}),
    .in_6({Dcurr[63:56], Din[7:0], Dcurr[47:0]}), .in_7({Din[7:0], Dcurr[55:0]}), .out(SB));

  // Other names for the same wires on the sheet: b0[7:0] = Dcurr[7:0]; b1[7:0] = Dcurr[15:8]; b2[7:0] = Dcurr[23:16];
  //   b3[7:0] = Dcurr[31:24]; b4[7:0] = Dcurr[39:32]; b5[7:0] = Dcurr[47:40]; b6[7:0] = Dcurr[55:48];
  //   b7[7:0] = Dcurr[63:56]
endmodule
