// Digital circuit SLLI.dig as structural Verilog
module SLLI (
  input  [6:0] opcode,
  input  [2:0] funct3,
  input  [5:0] funct6,
  output EQ
);

  wire comparator_1_eq, comparator_2_eq, comparator_3_eq;

  Comparator #(.Bits(7)) comparator_1 (.a(opcode), .b(7'b0010011), .eq(comparator_1_eq));  // open: gt, lt
  Comparator #(.Bits(3)) comparator_2 (.a(funct3), .b(3'b001), .eq(comparator_2_eq));  // open: gt, lt
  Comparator #(.Bits(6)) comparator_3 (.a(funct6), .b({6{1'b0}}), .eq(comparator_3_eq));  // open: gt, lt
  and and_1 (EQ, comparator_1_eq, comparator_2_eq, comparator_3_eq);
endmodule
