// Digital circuit SW.dig as structural Verilog
module SW (
  input  [63:0] Din,
  input  [63:0] Dcurr,
  input  byteInd,
  output [63:0] SW
);

  Multiplexer #(.Bits(64)) multiplexer_1 (
    .sel(byteInd), .in_0({Dcurr[63:32], Din[31:0]}), .in_1({Din[31:0], Dcurr[31:0]}), .out(SW));

  // Other names for the same wires on the sheet: b0[31:0] = Dcurr[31:0]; b1[31:0] = Dcurr[63:32]
endmodule
