// Digital circuit Save.dig as structural Verilog
module Save (
  input  [6:0] opcode,
  input  [2:0] funct3,
  output EQ
);

  wire comparator_1_eq, comparator_2_eq, comparator_3_eq, comparator_4_eq, or_1_out;

  Comparator #(.Bits(7)) comparator_1 (.a(opcode), .b(7'b0100011), .eq(comparator_1_eq));  // open: gt, lt
  Comparator #(.Bits(3)) comparator_2 (.a(funct3), .b(3'b000), .eq(comparator_2_eq));  // open: gt, lt
  Comparator #(.Bits(3)) comparator_3 (.a(funct3), .b(3'b010), .eq(comparator_3_eq));  // open: gt, lt
  Comparator #(.Bits(3)) comparator_4 (.a(funct3), .b(3'b011), .eq(comparator_4_eq));  // open: gt, lt
  or or_1 (or_1_out, comparator_2_eq, comparator_3_eq, comparator_4_eq);
  and and_1 (EQ, comparator_1_eq, or_1_out);
endmodule
