// Digital circuit WRITE.dig as structural Verilog
module WRITE (
  input  [63:0] ADDR,
  input  [63:0] Din,
  input  [63:0] Dcurr,
  input  [2:0] funct3,
  output [63:0] Dout
);

  wire [63:0] sb_1_sb, sw_1_sw;

  SB sb_1 (.byteInd(ADDR[2:0]), .Din(Din), .Dcurr(Dcurr), .SB(sb_1_sb));
  SW sw_1 (.byteInd(ADDR[2]), .Din(Din), .Dcurr(Dcurr), .SW(sw_1_sw));
  Multiplexer #(.Selector_Bits(2), .Bits(64)) multiplexer_1 (
    .sel(funct3[1:0]), .in_0(sb_1_sb), .in_1({64{1'b0}}), .in_2(sw_1_sw), .in_3(Din), .out(Dout));

  // Other names for the same wires on the sheet: addr0_2[2:0] = ADDR[2:0]
endmodule
