// Digital circuit inst_memory.dig as structural Verilog
module inst_memory (
  input  [7:0] ADDR,
  input  [4:0] PROG,
  output [31:0] IW
);

  wire [31:0] notconnected_1_out, notconnected_2_out, notconnected_3_out, notconnected_4_out,
       notconnected_5_out, notconnected_6_out, notconnected_7_out, notconnected_8_out, rom_1_d, rom_2_d,
       rom_3_d, rom_4_d, rom_5_d, rom_6_d, rom_7_d, rom_8_d, rom_9_d, rom_10_d, rom_11_d, rom_12_d, rom_13_d,
       rom_14_d, rom_15_d, rom_16_d, rom_17_d, rom_18_d, rom_19_d, rom_20_d, rom_21_d, rom_22_d, rom_23_d,
       rom_24_d;

  ROM #(.AddrBits(8), .Bits(32)) rom_1 (.A(ADDR), .sel(1'b1), .D(rom_1_d));
  ROM #(.AddrBits(8), .Bits(32)) rom_2 (.A(ADDR), .sel(1'b1), .D(rom_2_d));
  ROM #(.AddrBits(8), .Bits(32)) rom_3 (.A(ADDR), .sel(1'b1), .D(rom_3_d));
  ROM #(.AddrBits(8), .Bits(32)) rom_4 (.A(ADDR), .sel(1'b1), .D(rom_4_d));
  ROM #(.AddrBits(8), .Bits(32)) rom_5 (.A(ADDR), .sel(1'b1), .D(rom_5_d));
  ROM #(.AddrBits(8), .Bits(32)) rom_6 (.A(ADDR), .sel(1'b1), .D(rom_6_d));
  ROM #(.AddrBits(8), .Bits(32)) rom_7 (.A(ADDR), .sel(1'b1), .D(rom_7_d));
  ROM #(.AddrBits(8), .Bits(32)) rom_8 (.A(ADDR), .sel(1'b1), .D(rom_8_d));
  ROM #(.AddrBits(8), .Bits(32)) rom_9 (.A(ADDR), .sel(1'b1), .D(rom_9_d));
  ROM #(.AddrBits(8), .Bits(32)) rom_10 (.A(ADDR), .sel(1'b1), .D(rom_10_d));
  ROM #(.AddrBits(8), .Bits(32)) rom_11 (.A(ADDR), .sel(1'b1), .D(rom_11_d));
  ROM #(.AddrBits(8), .Bits(32)) rom_12 (.A(ADDR), .sel(1'b1), .D(rom_12_d));
  ROM #(.AddrBits(8), .Bits(32)) rom_13 (.A(ADDR), .sel(1'b1), .D(rom_13_d));
  ROM #(.AddrBits(8), .Bits(32)) rom_14 (.A(ADDR), .sel(1'b1), .D(rom_14_d));
  ROM #(.AddrBits(8), .Bits(32)) rom_15 (.A(ADDR), .sel(1'b1), .D(rom_15_d));
  ROM #(.AddrBits(8), .Bits(32)) rom_16 (.A(ADDR), .sel(1'b1), .D(rom_16_d));
  ROM #(.AddrBits(8), .Bits(32)) rom_17 (.A(ADDR), .sel(1'b1), .D(rom_17_d));
  ROM #(.AddrBits(8), .Bits(32)) rom_18 (.A(ADDR), .sel(1'b1), .D(rom_18_d));
  ROM #(.AddrBits(8), .Bits(32)) rom_19 (.A(ADDR), .sel(1'b1), .D(rom_19_d));
  ROM #(.AddrBits(8), .Bits(32)) rom_20 (.A(ADDR), .sel(1'b1), .D(rom_20_d));
  ROM #(.AddrBits(8), .Bits(32)) rom_21 (.A(ADDR), .sel(1'b1), .D(rom_21_d));
  ROM #(.AddrBits(8), .Bits(32)) rom_22 (.A(ADDR), .sel(1'b1), .D(rom_22_d));
  ROM #(.AddrBits(8), .Bits(32)) rom_23 (.A(ADDR), .sel(1'b1), .D(rom_23_d));
  ROM #(.AddrBits(8), .Bits(32)) rom_24 (.A(ADDR), .sel(1'b1), .D(rom_24_d));
  Multiplexer #(.Selector_Bits(5), .Bits(32)) multiplexer_1 (
    .sel(PROG), .in_0(rom_1_d), .in_1(rom_2_d), .in_2(rom_3_d), .in_3(rom_4_d), .in_4(rom_5_d),
    .in_5(rom_6_d), .in_6(rom_7_d), .in_7(rom_8_d), .in_8(rom_9_d), .in_9(rom_10_d), .in_10(rom_11_d),
    .in_11(rom_12_d), .in_12(rom_13_d), .in_13(rom_14_d), .in_14(rom_15_d), .in_15(rom_16_d),
    .in_16(rom_17_d), .in_17(rom_18_d), .in_18(rom_19_d), .in_19(rom_20_d), .in_20(rom_21_d),
    .in_21(rom_22_d), .in_22(rom_23_d), .in_23(rom_24_d), .in_24(notconnected_1_out),
    .in_25(notconnected_2_out), .in_26(notconnected_3_out), .in_27(notconnected_4_out),
    .in_28(notconnected_5_out), .in_29(notconnected_6_out), .in_30(notconnected_7_out),
    .in_31(notconnected_8_out), .out(IW));
  // NotConnected on notconnected_1_out
  // NotConnected on notconnected_2_out
  // NotConnected on notconnected_3_out
  // NotConnected on notconnected_4_out
  // NotConnected on notconnected_5_out
  // NotConnected on notconnected_6_out
  // NotConnected on notconnected_7_out
  // NotConnected on notconnected_8_out

  // Notes on the sheet:
  //   contents of rom_1 (hex, n*v repeats v):
  //   100513,200593,b50633,c0001073
  //   contents of rom_2 (hex, n*v repeats v):
  //   100513,250613,c0001073
  //   contents of rom_3 (hex, n*v repeats v):
  //   100593,200613,c59533,c0001073
  //   contents of rom_4 (hex, n*v repeats v):
  //   100593,359513,c0001073
  //   contents of rom_5 (hex, n*v repeats v):
  //   800593,100613,c5d533,c0001073
  //   contents of rom_6 (hex, n*v repeats v):
  //   2000593,25d513,c0001073
  //   contents of rom_7 (hex, n*v repeats v):
  //   8000113,ff810113,513,6300293,513023,13503,c0001073
  //   contents of rom_8 (hex, n*v repeats v):
  //   8000113,ff810113,513,6300293,512023,12503,c0001073
  //   contents of rom_9 (hex, n*v repeats v):
  //   100513,200593,8000ef,c0001073,b50533,8067
  //   contents of rom_10 (hex, n*v repeats v):
  //   100513,80006f,513,c0001073
  //   contents of rom_11 (hex, n*v repeats v):
  //   100513,100593,b50463,513,c0001073
  //   contents of rom_12 (hex, n*v repeats v):
  //   100513,200593,b54463,513,c0001073
  //   contents of rom_13 (hex, n*v repeats v):
  //   200513,100593,b55463,513,c0001073
  //   contents of rom_14 (hex, n*v repeats v):
  //   300513,300593,2b50533,c0001073
  //   contents of rom_15 (hex, n*v repeats v):
  //   1537,c0001073
  //   contents of rom_16 (hex, n*v repeats v):
  //   8000113,ff810113,513,6300293,5101a3,310503,c0001073
  //   contents of rom_17 (hex, n*v repeats v):
  //   200513,300593,400613,500693,8000ef,c0001073,2a502b3,2b282b3,2c50333
  //   ,628533,d50533,8067
  //   contents of rom_18 (hex, n*v repeats v):
  //   17537,fa55051b,c00593,f00613,8000ef,c0001073,40b602b3,128293,4000393
  //   ,729863,50313,fff00393,140006f,b55333,100393,5393b3,fff38393,737533,8067
  //   contents of rom_19 (hex, n*v repeats v):
  //   513,100593,200613,14000ef,c0001073,b55463,58513,8067,ff810113
  //   ,113023,fedff0ef,50593,60513,fe1ff0ef,13083,810113,8067
  //   contents of rom_20 (hex, n*v repeats v):
  //   40000113,a00513,8000ef,c0001073,100293,a2c463,8067,fe810113,113023
  //   ,a13423,fff50513,fe5ff0ef,a13823,813503,ffe50513,fd5ff0ef,1013303
  //   ,650533,13083,1810113,8067
  //   contents of rom_21 (hex, n*v repeats v):
  //   40000113,ff810113,7200293,510023,6100293,5100a3,6300293,510123
  //   ,6500293,5101a3,6300293,510223,6100293,5102a3,7200293,510323,103a3
  //   ,200533,593,600613,8000ef,c0001073,c5c663,100513,3c0006f,b502b3
  //   ,28283,c50333,30303,628663,513,200006f,ff810113,113023,158593
  //   ,fff60613,fc9ff0ef,13083,810113,8067
  //   contents of rom_22 (hex, n*v repeats v):
  //   40000113,ff810113,4600293,510023,6f00293,5100a3,6f00293,510123
  //   ,4200293,5101a3,6100293,510223,7200293,5102a3,10323,200533,ff810113
  //   ,2005b3,2004b3,3c000ef,913,293,800313,3800393,2628063,48e03,7e1e33
  //   ,1c96933,148493,128293,ff838393,fe5ff06f,1200533,c0001073,6100313
  //   ,7b00393,50283,2028063,62c663,72d463,fe028293,558023,150513,158593
  //   ,fe1ff06f,58023,8067
  //   contents of rom_23 (hex, n*v repeats v):
  //   40000113,fe010113,200293,512023,800293,512223,600293,512423,400293
  //   ,512623,a00293,512823,c00293,512a23,200533,2004b3,600593,84000ef
  //   ,513,4a283,2029293,556533,44a283,556533,593,84a283,2029293,55e5b3
  //   ,c4a283,55e5b3,613,104a283,2029293,566633,144a283,566633,c0001073
  //   ,e13,293,52303,2be0063,52383,63c663,e0293,38313,1e0e13,450513
  //   ,fe5ff06f,28513,8067,fc810113,113023,293,50313,e13,50e93,6b2d863
  //   ,513423,613823,713c23,3c13023,2a13423,2b13823,30513,405585b3,f91ff0ef
  //   ,50f93,3013583,2813503,2013e03,1813383,1013303,813283,5f8e33,2e1f93
  //   ,1f50eb3,32383,eaf03,7f4663,7ea023,1e32023,128293,430313,f95ff06f
  //   ,13083,3810113,8067
  //   contents of rom_24 (hex, n*v repeats v):
  //   40000113,ff810113,3600293,510023,3500293,5100a3,510123,510223
  //   ,3300293,5101a3,293,5102a3,10513,a00593,5c000ef,c0001073,293,100313
  //   ,4060263,50383,6100e13,1c3c663,fa938393,180006f,4100e13,1c3c663
  //   ,fc938393,80006f,fd038393,2638e33,1c282b3,2b30333,fff60613,fff50513
  //   ,fc1ff06f,28513,8067,ff810113,113023,613,50303,30863,160613,150513
  //   ,ff1ff06f,fff50513,f89ff0ef,13083,810113,8067
endmodule
