// Digital circuit project06.dig as structural Verilog
module project06 (
  input  CLK,
  input  EN,
  input  CLR,
  input  [4:0] PROG,
  output [63:0] A0,
  output [63:0] A1,
  output [63:0] A2,
  output DONE,
  output [63:0] zero,
  output [63:0] ra,
  output [63:0] sp,
  output [63:0] gp,
  output [63:0] tp,
  output [63:0] t0,
  output [63:0] t1,
  output [63:0] t2,
  output [63:0] s0_fp,
  output [63:0] s1,
  output [63:0] a0_2,
  output [63:0] a1_2,
  output [63:0] a2_2,
  output [63:0] a3,
  output [63:0] a4,
  output [63:0] a5,
  output [63:0] a6,
  output [63:0] a7,
  output [63:0] s2,
  output [63:0] s3,
  output [63:0] s4,
  output [63:0] s5,
  output [63:0] s6,
  output [63:0] s7,
  output [63:0] s8,
  output [63:0] s9,
  output [63:0] s10,
  output [63:0] s11,
  output [63:0] t3,
  output [63:0] t4,
  output [63:0] t5,
  output [63:0] t6
);

  wire ALUSrcA, and_2_out, CLK_t, LD, MR, PCBr, PCsel, RFW, STR, WDsel;
  wire [2:0] ALUOp, ALUSrcB, BrOp, funct3;
  wire [4:0] rd, rs1, rs2;
  wire [31:0] iw;
  wire [63:0] alu_1_r, imm_I, immdecoder_1_imm_b, immdecoder_1_imm_j, immdecoder_1_imm_s, immdecoder_1_imm_u,
       multiplexer_1_out, multiplexer_2_out, multiplexer_3_out, multiplexer_4_out, multiplexer_5_out, PC,
       PC__plus__4_s, ramdualport_1_d, read_cir_1_dcurr, read_cir_1_dout, register_file_1_rd0,
       register_file_1_rd1, write_1_dout;

  Multiplexer #(.Bits(64)) multiplexer_1 (.sel(PCBr), .in_0(PC__plus__4_s), .in_1(alu_1_r), .out(multiplexer_1_out));
  Comparator #(.Bits(32)) comparator_1 (.a(iw), .b(32'hc0001073), .eq(DONE));  // open: gt, lt
  // _64_reg_clr _64_reg_clr_1: pin names not known; wires that end beside it: multiplexer_1_out, CLK_t, EN, CLR, PC
  and and_1 (CLK_t, CLK, ~DONE);  // And
  LED led_1 (.in(DONE));
  // Probe on PC
  // Probe on iw
  // Probe on rs1
  // Probe on rs2
  // Probe on rd
  // Probe on imm_I
  inst_memory inst_memory_1 (.PROG(PROG), .ADDR(PC[9:2]), .IW(iw));
  Add #(.Bits(64)) PC__plus__4 (.a(PC), .b(64'h4), .c_i(1'b0), .s(PC__plus__4_s));  // open: c_o
  // Probe on iw
  InstrDecoder instrdecoder_1 (
    .IW(iw), .LD(LD), .STR(STR), .MR(MR), .BrOp(BrOp), .WDSel(WDsel), .PCSel(PCsel), .ALUSrcB(ALUSrcB),
    .ALUSrcA(ALUSrcA), .ALUOp(ALUOp), .RFW(RFW), .funct3(funct3));
  RegDecoder regdecoder_1 (.IW(iw), .RS1(rs1), .RS2(rs2), .RD(rd));
  ImmDecoder immdecoder_1 (
    .IW(iw), .imm_I(imm_I), .imm_S(immdecoder_1_imm_s), .imm_B(immdecoder_1_imm_b),
    .imm_U(immdecoder_1_imm_u), .imm_J(immdecoder_1_imm_j));
  Multiplexer #(.Bits(64)) multiplexer_2 (
    .sel(WDsel), .in_0(multiplexer_5_out), .in_1(PC__plus__4_s), .out(multiplexer_2_out));
  and and_2 (and_2_out, RFW, EN);
  register_file register_file_1 (
    .ReadReg0(rs1), .ReadReg1(rs2), .WriteData(multiplexer_2_out), .CLK(CLK_t), .WriteEn(and_2_out),
    .CLR(CLR), .WriteReg(rd), .RD0(register_file_1_rd0), .RD1(register_file_1_rd1), .x0(zero), .x1(ra),
    .x2(sp), .x3(gp), .x4(tp), .x5(t0), .x6(t1), .x7(t2), .x8(s0_fp), .x9(s1), .x10(A0), .x11(A1), .x12(A2),
    .x13(a3), .x14(a4), .x15(a5), .x16(a6), .x17(a7), .x18(s2), .x19(s3), .x20(s4), .x21(s5), .x22(s6),
    .x23(s7), .x24(s8), .x25(s9), .x26(s10), .x27(s11), .x28(t3), .x29(t4), .x30(t5), .x31(t6));
  // Probe on register_file_1_rd1
  // Probe on register_file_1_rd0
  Multiplexer #(.Bits(64)) multiplexer_3 (
    .sel(ALUSrcA), .in_0(register_file_1_rd0), .in_1(PC), .out(multiplexer_3_out));
  Multiplexer #(.Selector_Bits(3), .Bits(64)) multiplexer_4 (
    .sel(ALUSrcB), .in_0(register_file_1_rd1), .in_1(imm_I), .in_2(immdecoder_1_imm_j),
    .in_3(immdecoder_1_imm_b), .in_4(immdecoder_1_imm_s), .in_5(immdecoder_1_imm_u), .in_6({64{1'b0}}),
    .in_7({64{1'b0}}), .out(multiplexer_4_out));
  // BranchUnit branchunit_1: pin names not known; wires that end beside it: register_file_1_rd0, register_file_1_rd1, funct3, PCsel, BrOp, PCBr
  // Probe on ALUOp
  alu alu_1 (.A(multiplexer_3_out), .B(multiplexer_4_out), .ALUOp(ALUOp), .R(alu_1_r));
  Multiplexer #(.Bits(64)) multiplexer_5 (.sel(MR), .in_0(alu_1_r), .in_1(read_cir_1_dout), .out(multiplexer_5_out));
  // Probe on alu_1_r
  WRITE write_1 (
    .ADDR(alu_1_r), .Din(register_file_1_rd1), .Dcurr(read_cir_1_dcurr), .funct3(funct3), .Dout(write_1_dout));
  // Probe on alu_1_r[9:3]
  RAMDualPort #(.AddrBits(7), .Bits(64)) ramdualport_1 (
    .A(alu_1_r[9:3]), .Din(write_1_dout), .str(STR), .C(CLK_t), .ld(LD), .D(ramdualport_1_d));
  READ_CIR read_cir_1 (
    .A(alu_1_r), .Din(ramdualport_1_d), .funct3(funct3), .Dout(read_cir_1_dout), .Dcurr(read_cir_1_dcurr));

  assign a0_2 = A0;
  assign a1_2 = A1;
  assign a2_2 = A2;

  // Other names for the same wires on the sheet: x0[63:0] = zero; x1[63:0] = ra; x2[63:0] = sp; x3[63:0] = gp;
  //   x4[63:0] = tp; x5[63:0] = t0; x6[63:0] = t1; x7[63:0] = t2; x8[63:0] = s0_fp; x9[63:0] = s1; x10[63:0] = A0;
  //   x11[63:0] = A1; x12[63:0] = A2; x13[63:0] = a3; x14[63:0] = a4; x15[63:0] = a5; x16[63:0] = a6; x17[63:0] = a7;
  //   x18[63:0] = s2; x19[63:0] = s3; x20[63:0] = s4; x21[63:0] = s5; x22[63:0] = s6; x23[63:0] = s7; x24[63:0] = s8;
  //   x25[63:0] = s9; x26[63:0] = s10; x27[63:0] = s11; x28[63:0] = t3; x29[63:0] = t4; x30[63:0] = t5;
  //   x31[63:0] = t6
endmodule

/* Test case 00-add-r:
CLR EN CLK PROG A2
1   0   0   x    x
0   0   0   x    x
while (!(DONE))
0   1   C   0    x
end while
0   1   0   0    3
*/

/* Test case 01-add-r:
CLR EN CLK PROG A2
1   0   0   x    x
0   0   0   x    x
while (!(DONE))
0   1   C   1    x
end while
0   1   1   1    3
*/

/* Test case 02-sll-r:
CLR EN CLK PROG A0
1   0   0   x    x
0   0   0   x    x
while (!(DONE))
0   1   C   2    x
end while
0   1   0   2    4
*/

/* Test case 03-sll-i:
CLR EN CLK PROG A0
1   0   0   x    x
0   0   0   x    x
while (!(DONE))
0   1   C   3    x
end while
0   1   0   3    8
*/

/* Test case 04-srl-r:
CLR EN CLK PROG A0
1   0   0   x    x
0   0   0   x    x
while (!(DONE))
0   1   C   4    x
end while
0   1   0   4    4
*/

/* Test case 05-srl-i:
CLR EN CLK PROG A0
1   0   0   x    x
0   0   0   x    x
while (!(DONE))
0   1   C   5    x
end while
0   1   0   5    8
*/

/* Test case 06-sd-ld:
CLR EN CLK PROG A0
1   0   0   x    x
0   0   0   x    x
while (!(DONE))
0   1   C   6    x
end while
0   1   0   6    99
*/

/* Test case 07-sw-lw:
CLR EN CLK PROG A0
1   0   0   x    x
0   0   0   x    x
while (!(DONE))
0   1   C   7    x
end while
0   1   0   7    99
*/

/* Test case 08-jal:
EN CLR CLK PROG A0
1  1   0   x    x
1  0   0   x    x
while (!(DONE))
1  0   C   8    x
end while
1  0   0   8    3
*/

/* Test case 09-j:
EN CLR CLK PROG A0
1  1   0   x    x
1  0   0   x    x
while (!(DONE))
1  0   C   9    x
end while
1  0   0   9    1
*/

/* Test case 10-beq:
EN CLR CLK PROG A0
1  1   0   x    x
1  0   0   x    x
while (!(DONE))
1  0   C   10   x
end while
1  0   0   10   1
*/

/* Test case 11-blt:
EN CLR CLK PROG A0
1  1   0   x    x
1  0   0   x    x
while (!(DONE))
1  0   C   11   x
end while
1  0   0   11   1
*/

/* Test case 12-bge:
EN CLR CLK PROG A0
1  1   0   x    x
1  0   0   x    x
while (!(DONE))
1  0   C   12   x
end while
1  0   0   12   2
*/

/* Test case 13-mul:
EN CLR CLK PROG A0
1  1   0   x    x
1  0   0   x    x
while (!(DONE))
1  0   C   13   x
end while
1  0   0   13   9
*/

/* Test case 14-lui:
EN CLR CLK PROG A0
1  1   0   x    x
1  0   0   x    x
while (!(DONE))
1  0   C   14   x
end while
1  0   0   14   4096
*/

/* Test case 15-sb-lb:
CLR EN CLK PROG A0
1   0   0   x    x
0   0   0   x    x
while (!(DONE))
0   1   C   15    x
end while
0   1   0   15    99
*/

/* Test case 16-quadratic:
CLR EN CLK PROG A0
1   0   0   x    x
0   0   0   x    x
while (!(DONE))
0   1   C   16    x
end while
0   1   0   16    25
*/

/* Test case 17-getbitseq:
CLR EN CLK PROG A0
1   0   0   x    x
0   0   0   x    x
while (!(DONE))
0   1   C   17   x
end while
0   1   0   17   6
*/

/* Test case 18-max3:
CLR EN CLK PROG A0
1   0   0   x    x
0   0   0   x    x
while (!(DONE))
0   1   C   18   x
end while
0   1   0   18   2
*/

/* Test case 19-fibrec:
CLR EN CLK PROG A0
1   0   0   x    x
0   0   0   x    x
while (!(DONE))
0   1   C   19   x
end while
0   1   0   19   55
*/

/* Test case 20-ispal:
CLR EN CLK PROG A0
1   0   0   x    x
0   0   0   x    x
while (!(DONE))
0   1   C   20   x
end while
0   1   0   20   1
*/

/* Test case 21-toUpper:
CLR EN CLK PROG A0
1   0   0   x    x
0   0   0   x    x
while (!(DONE))
0   1   C   21   x
end while
0   1   0   21   5066355251797426176
*/

/* Test case 22-sort:
CLR EN CLK PROG A0 A1 A2
1   0   0   x    x    x    x
0   0   0   x    x    x    x
while (!(DONE))
0   1   C   22   x    x    x
end while
0   1   0   22   51539607562 34359738374 17179869186
*/

/* Test case 23-str-to-int:
CLR EN CLK PROG A0 A1 A2
1   0   0   x    x    x    x
0   0   0   x    x    x    x
while (!(DONE))
0   1   C   23   x    x    x
end while
0   1   0   23   65535 x x
*/
