// Digital circuit hazardUnit.dig as structural Verilog
module hazardUnit (
  input  [4:0] RR0_2,
  input  [4:0] RR1_2,
  input  [4:0] WR_3,
  input  RFW_3,
  input  [4:0] WR_4,
  input  RFW_4,
  input  PC_Br_2,
  output [1:0] FRD0sel,
  output [1:0] FRD1sel,
  output FLS_IF,
  output FLS_DR
);

  wire and_1_out, and_2_out, and_3_out, and_4_out, comparator_1_eq, comparator_2_eq, comparator_3_eq,
       comparator_4_eq;

  Comparator #(.Bits(5)) comparator_1 (.a(RR0_2), .b(WR_4), .eq(comparator_1_eq));  // open: gt, lt
  Comparator #(.Bits(5)) comparator_2 (.a(RR0_2), .b(WR_3), .eq(comparator_2_eq));  // open: gt, lt
  Comparator #(.Bits(5)) comparator_3 (.a(RR1_2), .b(WR_4), .eq(comparator_3_eq));  // open: gt, lt
  Comparator #(.Bits(5)) comparator_4 (.a(RR1_2), .b(WR_3), .eq(comparator_4_eq));  // open: gt, lt
  and and_1 (and_1_out, RFW_4, comparator_1_eq);
  and and_2 (and_2_out, RFW_3, comparator_2_eq);
  and and_3 (and_3_out, RFW_4, comparator_3_eq);
  and and_4 (and_4_out, RFW_3, comparator_4_eq);
  PriorityEncoder #(.Selector_Bits(2)) priorityencoder_1 (
    .in0(1'b1), .in1(and_1_out), .in2(and_2_out), .in3(1'b0), .num(FRD0sel));  // open: any
  PriorityEncoder #(.Selector_Bits(2)) priorityencoder_2 (
    .in0(1'b1), .in1(and_3_out), .in2(and_4_out), .in3(1'b0), .num(FRD1sel));  // open: any

  assign FLS_DR = PC_Br_2;
  assign FLS_IF = PC_Br_2;
endmodule
